# Fritzing sketch mbed_OS_5_Thread_Test (saved by Fritzing 0.9.3b)
breadboards: 1

parts:
  J1 = STM32 Nucleo boards
  R1 = Rotary Potentiometer (Small) [maximum_resistance=100kΩ package=THT]
  R2 = Rotary Potentiometer (Small) [maximum_resistance=100kΩ package=THT]
  C1 = Electrolytic Capacitor [capacitance=1µF package="100 mil [THT, electrolytic]"]
  C2 = Ceramic Capacitor [capacitance=100nF package="100 mil [THT, multilayer]"]
  U1 = mystery part, 4 pins [chip_label=SSD1306]

nets:
  N1: J1.A0, R1.wiper
  N2: J1.A1, R2.wiper
  N3: J1.A4/SDA, U1.pin1
  N4: J1.A5/SCL, U1.pin2
  N5: J1.3V3, R1.leg2, R2.leg2, C1.+, C2.1, U1.pin3
  N6: J1.GND, R1.leg1, R2.leg1, C1.-, C2.0, U1.pin4

notes:
  OUT
  Freq
  Amp
